# Fritzing sketch Totalizer (saved by Fritzing 0.9.3b)

parts:
  M1 = ESP32-S2-DevKitC-1 [part_number=ESP32-S2-DevKitC-1]
  U1 = LM2596 step down module
  J1 = Screw terminal - 2 pins [package=THT]
  A1 = 2 channel relay module [package=THT]

nets:
  N1: M1.pin_21, U1.OUT+, A1.pin_13
  N2: M1.pin_22, U1.IN-, U1.OUT-, J1.pin1, A1.pin_14
  N3: M1.pin_39, A1.pin_15
  N4: U1.IN+, J1.pin2

notes:
  ESP Pin 2 = Relay Input 1
  ESP Pin 5 = Pulse Input

custom parts:
  ESP32-S2-DevKitC-1: ESP32-S2-DevKitC-1 is an entry-level development board based on ESP32-S2-SOLO (on-board PCB antenna). It is based on the ESP32 microcontroller that boasts Wifi, Bluetooth, Ethernet and Low Power support all in a single chip. (vanepp) Feb 2022: converted to ESP32-S2-DevKitC-1. This module is 44pins long (2x22) and 11 pins width.
  LM2596 step down module: LM2596 DC-DC step down power supply module 3 A.
  2 channel relay module: 2 channel Relay Module 5V 12V 24V High and Low Level Trigger Relay Control With Optocoupler Two Way relays DC 5 V 12 V 24 V Volt.
